# Fritzing sketch ProjektOdległości (saved by Fritzing 0.9.3b)
breadboards: 1

parts:
  Grove1 = Grove OLED 128x96
  Part1 = Arduino Nano (Rev3.0) (ICSP)
  hc-sr1 = hc-sr04
  LED1 = LEDs [package=led10mm]
  S1 = Square Pushbutton
  U1 = LIPO-110mAh [package=lipo-110]
  S2 = Round Pushbutton

nets:
  GND: Grove1.GND, Part1.GND, hc-sr1.GND, LED1.A, S1.leg0, U1.-
  VCC: Grove1.VCC, Part1.5V, hc-sr1.VCC
  N1: Grove1.SDA, Part1.A4
  N2: Grove1.SCL, Part1.A5
  N3: Part1.D5, LED1.C
  N4: Part1.D8, hc-sr1.Echo
  N5: Part1.D9, hc-sr1.Trig
  N6: Part1.D10, S1.leg1
  N7: Part1.VIN, S2.leg0
  N8: U1.+, S2.leg1
